// Logisim project Trabalho Neto Guilherme M. Lemos.circ as structural Verilog: 1 circuit, main circuit Trabalho neto 
module Trabalho_neto (
  input  A,
  input  B,
  input  C,
  output S_1,
  output S_2,
  output S_3,
  output S_4,
  output S_5
);

  wire and_1_out, and_2_out, and_3_out, and_4_out, and_5_out, and_6_out, and_7_out, and_8_out, and_9_out,
       and_10_out, and_11_out, and_12_out, and_13_out, not_1_out, not_2_out, not_3_out, not_4_out, not_5_out,
       not_6_out, not_7_out, not_8_out, not_9_out, not_10_out, not_11_out, not_12_out, not_13_out,
       not_14_out, not_15_out, not_16_out;

  not not_1 (not_1_out, A);
  not not_2 (not_2_out, C);
  not not_3 (not_3_out, B);
  not not_4 (not_4_out, B);
  not not_5 (not_5_out, C);
  not not_6 (not_6_out, B);
  not not_7 (not_7_out, C);
  not not_8 (not_8_out, A);
  not not_9 (not_9_out, B);
  not not_10 (not_10_out, C);
  not not_11 (not_11_out, C);
  not not_12 (not_12_out, A);
  not not_13 (not_13_out, C);
  not not_14 (not_14_out, A);
  not not_15 (not_15_out, C);
  not not_16 (not_16_out, B);
  and and_1 (and_1_out, not_1_out, not_2_out);
  and and_2 (and_2_out, B, C);
  and and_3 (and_3_out, A, not_3_out);
  or or_1 (S_2, not_4_out, not_5_out);
  and and_4 (and_4_out, not_6_out, C);
  and and_5 (and_5_out, A, not_7_out);
  and and_6 (and_6_out, not_8_out, not_9_out, C);
  and and_7 (and_7_out, B, not_10_out);
  and and_8 (and_8_out, A, not_11_out);
  and and_9 (and_9_out, A, B);
  and and_10 (and_10_out, not_12_out, not_13_out);
  and and_11 (and_11_out, not_14_out, B);
  and and_12 (and_12_out, B, not_15_out);
  and and_13 (and_13_out, A, not_16_out, C);
  or or_2 (S_1, and_1_out, and_2_out, and_3_out);
  or or_3 (S_3, and_4_out, and_5_out);
  or or_4 (S_4, and_6_out, and_7_out, and_8_out, and_9_out);
  or or_5 (S_5, and_10_out, and_11_out, and_12_out, and_13_out);
endmodule
